// Logisim project NAND_equivalences.circ as structural Verilog: 1 circuit, main circuit main
module main (
);

  wire and_1_out, nand_1_out, nand_2_out, nand_3_out, nand_4_out, nand_5_out, nand_6_out, nor_1_out,
       nor_2_out, nor_3_out, nor_4_out, nor_5_out, nor_6_out, not_1_out, or_1_out, undriven, undriven_2,
       undriven_3, undriven_4, undriven_5, undriven_6, undriven_7, undriven_8, undriven_9;

  not not_1 (not_1_out, undriven);
  and and_1 (and_1_out, undriven_2, undriven_3);
  // OR_Gate or_1 has open pins: out=or_1_out
  nor nor_1 (nor_1_out, undriven_4, undriven_4);
  nor nor_2 (nor_2_out, undriven_5, undriven_5);
  // NOR_Gate nor_3 has open pins: out=nor_3_out
  nor nor_4 (nor_4_out, undriven_6, undriven_6);
  nor nor_5 (nor_5_out, nor_1_out, nor_2_out);
  // NOR_Gate nor_6 has open pins: out=nor_6_out
  nand nand_1 (nand_1_out, undriven_7, undriven_8);
  // NAND_Gate nand_2 has open pins: out=nand_2_out
  // NAND_Gate nand_3 has open pins: out=nand_3_out
  nand nand_4 (nand_4_out, undriven_9, undriven_9);
  nand nand_5 (nand_5_out, nand_1_out, nand_1_out);
  // NAND_Gate nand_6 has open pins: out=nand_6_out

  // Notes on the sheet:
  //   a
  //   a
  //   b
  //   a
  //   b
  //   b
  //   a
  //   b
  //   a
  //   b
  //   a
  //   b
  //   a
  //   b
  //   a
  //   b
  //   a
  //   b
endmodule
