// Logisim project display7seg.circ as structural Verilog
module sss (
  input  x,
  input  y,
  input  z,
  input  k,
  output a,
  output b,
  output c,
  output d,
  output e,
  output f,
  output g
);

  or or_1 (g, z, y, x);

  assign a = 1'b1;
  assign b = 1'b1;
  assign c = 1'b1;
  assign d = 1'b1;
  assign e = 1'b1;
  assign f = 1'b1;
endmodule

module s (
  input  x,
  input  y,
  input  z,
  input  k,
  output a,
  output b,
  output c,
  output d,
  output e,
  output f,
  output g
);

  wire and_1_out, and_2_out, and_3_out, and_4_out, and_5_out, and_6_out, and_7_out, and_8_out, and_9_out,
       and_10_out, and_11_out, and_12_out, and_13_out, and_14_out, and_15_out, and_16_out, and_17_out,
       and_18_out, and_19_out, and_20_out, and_21_out, and_22_out, and_23_out, and_24_out, and_25_out,
       not_1_out, not_2_out, not_3_out, not_4_out;

  not not_1 (not_1_out, x);
  not not_2 (not_2_out, y);
  not not_3 (not_3_out, z);
  not not_4 (not_4_out, k);
  and and_1 (and_1_out, not_2_out, not_4_out);
  and and_2 (and_2_out, not_1_out, z);
  and and_3 (and_3_out, y, k);
  and and_4 (and_4_out, x, not_3_out);
  and and_5 (and_5_out, not_3_out, not_4_out);
  and and_6 (and_6_out, x, not_3_out);
  and and_7 (and_7_out, not_1_out, z, k);
  and and_8 (and_8_out, not_2_out, not_4_out);
  and and_9 (and_9_out, not_3_out, not_4_out);
  and and_10 (and_10_out, not_1_out, z, k);
  and and_11 (and_11_out, x, not_3_out);
  and and_12 (and_12_out, x, not_4_out);
  and and_13 (and_13_out, not_2_out, not_4_out);
  and and_14 (and_14_out, not_1_out, not_2_out, z);
  and and_15 (and_15_out, y, not_3_out, k);
  and and_16 (and_16_out, z, not_4_out);
  and and_17 (and_17_out, not_1_out, not_2_out, not_3_out);
  and and_18 (and_18_out, z, not_4_out);
  and and_19 (and_19_out, x, z);
  and and_20 (and_20_out, not_2_out, not_4_out);
  and and_21 (and_21_out, y, not_4_out);
  and and_22 (and_22_out, y, not_3_out);
  and and_23 (and_23_out, x, not_3_out);
  and and_24 (and_24_out, not_1_out, not_2_out, z);
  and and_25 (and_25_out, not_1_out, z, not_4_out);
  or or_1 (a, and_1_out, and_2_out, and_3_out, and_4_out);
  or or_2 (b, and_5_out, and_6_out, and_7_out, and_8_out);
  or or_3 (c, and_9_out, and_10_out, y, and_11_out, and_12_out);
  or or_4 (d, and_13_out, and_14_out, and_15_out, and_16_out);
  or or_5 (e, and_17_out, and_18_out, and_19_out, and_20_out);
  or or_6 (f, not_3_out, and_21_out, x);
  or or_7 (g, and_22_out, and_23_out, and_24_out, and_25_out);
endmodule

module DDD (
  input  x,
  input  y
);

  wire and_1_out, and_2_out, not_1_out, not_2_out, or_1_out, or_2_out, or_3_out, or_4_out, or_5_out;

  not not_1 (not_1_out, x);
  not not_2 (not_2_out, y);
  or or_1 (or_1_out, not_2_out, x);
  or or_2 (or_2_out, not_2_out, x);
  and and_1 (and_1_out, not_1_out, not_2_out);
  and and_2 (and_2_out, x, y);
  or or_3 (or_3_out, not_2_out, x);
  or or_4 (or_4_out, not_1_out, not_2_out);
  or or_5 (or_5_out, and_1_out, and_2_out);
  _7_Segment_Display u_7_segment_display_1 (
    .g(x), .f(not_1_out), .a(or_1_out), .b(or_2_out), .e(or_4_out), .d(or_3_out), .c(or_5_out));  // open: dp
endmodule
