// Logisim project exercicio.circ as structural Verilog
module sa (
  input  x,
  input  y,
  input  z,
  output f
);

  wire and_1_out, and_2_out, not_1_out, not_2_out, not_3_out, or_1_out;

  not not_1 (not_1_out, x);
  not not_2 (not_2_out, y);
  not not_3 (not_3_out, z);
  and and_1 (and_1_out, y, z);
  or or_1 (or_1_out, and_1_out, not_2_out, and_2_out);
  and and_2 (and_2_out, not_1_out, z);
  and and_3 (f, x, not_3_out, or_1_out);
endmodule

module ss (
  input  x,
  input  y,
  input  z,
  output f
);

  wire and_1_out, and_2_out, and_3_out, not_1_out, not_2_out, not_3_out;

  not not_1 (not_1_out, y);
  not not_2 (not_2_out, z);
  not not_3 (not_3_out, x);
  and and_1 (and_1_out, x, not_1_out, not_2_out);
  and and_2 (and_2_out, not_3_out, z);
  and and_3 (and_3_out, z, y);
  or or_1 (f, and_1_out, and_2_out, and_3_out);
endmodule
