// Logisim project mutiplexador.circ as structural Verilog: 1 circuit, main circuit main
module main (
  input  Ent3,
  input  Ent2,
  input  Ent1,
  input  Ent0,
  input  SelA,
  input  SelB,
  input  Enbl,
  output Saida
);

  wire and_1_out, and_2_out, and_3_out, and_4_out, not_1_out, not_2_out, not_3_out, not_4_out, not_5_out,
       or_1_out;

  not not_1 (not_1_out, SelA);
  not not_2 (not_2_out, SelB);
  not not_3 (not_3_out, SelA);
  not not_4 (not_4_out, SelB);
  and and_1 (and_1_out, not_1_out, Ent0, not_2_out);
  and and_2 (and_2_out, not_3_out, Ent1, SelB);
  and and_3 (and_3_out, SelA, Ent2, not_4_out);
  and and_4 (and_4_out, SelA, Ent3, SelB);
  not not_5 (not_5_out, Enbl);
  or or_1 (or_1_out, and_1_out, and_2_out, and_3_out, and_4_out);
  and and_5 (Saida, or_1_out, not_5_out);
endmodule
