// Logisim project somador (Copiar).circ as structural Verilog: 1 circuit, main circuit somador
module somador (
  input  a,
  input  b,
  input  Cin,
  output SUM,
  output Cout
);

  wire and_1_out, and_2_out, and_3_out, undriven, undriven_2, xor_1_out, xor_3_out;

  xor xor_1 (xor_1_out, a, b);
  and and_1 (and_1_out, a, b);
  and and_2 (and_2_out, a, Cin);
  and and_3 (and_3_out, b, Cin);
  xor xor_2 (SUM, xor_1_out, Cin);
  or or_1 (Cout, and_1_out, and_2_out, and_3_out);
  xor xor_3 (xor_3_out, undriven, undriven_2);
endmodule
