// Logisim project somadorCompletoGambiarra.circ as structural Verilog: 1 circuit, main circuit somadorCompleto
module somadorCompleto (
  input  Cin,
  input  a,
  input  b,
  output Sum,
  output Cout
);

  wire main_1_cout, main_1_sum, main_2_cout;

  somadorIncompleto_main main_1 (.a(a), .b(b), .Sum(main_1_sum), .Cout(main_1_cout));
  somadorIncompleto_main main_2 (.a(Cin), .b(main_1_sum), .Sum(Sum), .Cout(main_2_cout));
  or or_1 (Cout, main_2_cout, main_1_cout);
endmodule
