// Logisim project somadorCompletoParte01.circ as structural Verilog: 1 circuit, main circuit main
module main (
  input  a,
  input  b,
  input  Cin,
  output Sum
);

  wire xor_1_out;

  xor xor_1 (xor_1_out, a, b);
  xor xor_2 (Sum, xor_1_out, Cin);
endmodule
