// Logisim project somadorCompletoParte02.circ as structural Verilog: 1 circuit, main circuit main
module main (
  input  a,
  input  b,
  input  Cin,
  output Cout
);

  wire and_1_out, and_2_out, and_3_out;

  and and_1 (and_1_out, a, b);
  and and_2 (and_2_out, a, Cin);
  and and_3 (and_3_out, b, Cin);
  or or_1 (Cout, and_1_out, and_2_out, and_3_out);
endmodule
