// Logisim project somadorIncompleto.circ as structural Verilog: 1 circuit, main circuit main
module main (
  input  a,
  input  b,
  output Sum,
  output Cout
);

  xor xor_1 (Sum, a, b);
  and and_1 (Cout, a, b);
endmodule
