// Logisim project somadorUso.circ as structural Verilog: 2 circuits, main circuit somador4bits
module somador4bits (
  input  C0,
  input  a3,
  input  a2,
  input  a1,
  input  a0,
  input  b3,
  input  b2,
  input  b1,
  input  b0,
  output out_10,
  output out_11,
  output out_12,
  output out_13,
  output out_14
);

  wire somador_1_p6, somador_2_p6, somador_3_p6;

  // somador somador_1: pin names not known; wires that end beside it: a0, b0, a1, C0, out_14, somador_1_p6
  // somador somador_2: pin names not known; wires that end beside it: a1, b1, a2, somador_1_p6, out_13, somador_2_p6
  // somador somador_3: pin names not known; wires that end beside it: a2, b2, a3, somador_2_p6, out_12, somador_3_p6
  // somador somador_4: pin names not known; wires that end beside it: b3, b2, b1, b0, a3, b3, somador_3_p6, out_11, out_10
endmodule

module somador8bits (
  input  oprtn,
  output ovflw,
  output [7:0] res
);

  wire somador_1_p6, somador_2_p7, somador_3_p7, somador_4_p7, somador_5_p7, somador_6_p7, somador_7_p7,
       xor_1_out, xor_2_out, xor_3_out, xor_4_out, xor_5_out, xor_6_out, xor_7_out, xor_8_out;
  wire [7:0] a_out, b_out;

  Slider a (.out(a_out));
  Slider b (.out(b_out));
  xor xor_1 (xor_1_out, b_out[0], oprtn);
  xor xor_2 (xor_2_out, b_out[1], oprtn);
  xor xor_3 (xor_3_out, b_out[2], oprtn);
  xor xor_4 (xor_4_out, b_out[3], oprtn);
  xor xor_5 (xor_5_out, b_out[4], oprtn);
  xor xor_6 (xor_6_out, b_out[5], oprtn);
  xor xor_7 (xor_7_out, b_out[6], oprtn);
  xor xor_8 (xor_8_out, b_out[7], oprtn);
  // somador somador_1: pin names not known; wires that end beside it: a_out[0], xor_1_out, a_out[1], oprtn, res[0], somador_1_p6
  // somador somador_2: pin names not known; wires that end beside it: xor_1_out, a_out[1], xor_2_out, a_out[2], somador_1_p6, res[1], somador_2_p7
  // somador somador_3: pin names not known; wires that end beside it: xor_2_out, a_out[2], xor_3_out, a_out[3], somador_2_p7, res[2], somador_3_p7
  // somador somador_4: pin names not known; wires that end beside it: xor_3_out, a_out[3], xor_4_out, a_out[4], somador_3_p7, res[3], somador_4_p7
  // somador somador_5: pin names not known; wires that end beside it: xor_4_out, a_out[4], xor_5_out, a_out[5], somador_4_p7, res[4], somador_5_p7
  // somador somador_6: pin names not known; wires that end beside it: xor_5_out, a_out[5], xor_6_out, a_out[6], somador_5_p7, res[5], somador_6_p7
  // somador somador_7: pin names not known; wires that end beside it: xor_6_out, a_out[6], xor_7_out, a_out[7], somador_6_p7, res[6], somador_7_p7
  // somador somador_8: pin names not known; wires that end beside it: b_out[0], xor_7_out, a_out[7], xor_8_out, somador_7_p7, res[7], ovflw
endmodule
