// Logisim project subtratorCompletoParte01.circ as structural Verilog: 1 circuit, main circuit main
module main (
  input  a,
  input  b,
  input  Bin,
  output Diff
);

  wire xor_1_out;

  xor xor_1 (xor_1_out, a, b);
  xor xor_2 (Diff, xor_1_out, Bin);
endmodule
