// Logisim project subtratorCompletoParte02.circ as structural Verilog: 1 circuit, main circuit main
module main (
  input  a,
  input  b,
  input  Bin,
  output Bout
);

  wire and_1_out, and_2_out, and_3_out, not_1_out, not_2_out;

  not not_1 (not_1_out, a);
  not not_2 (not_2_out, a);
  and and_1 (and_1_out, not_1_out, b);
  and and_2 (and_2_out, not_2_out, Bin);
  and and_3 (and_3_out, b, Bin);
  or or_1 (Bout, and_1_out, and_2_out, and_3_out);
endmodule
