// Logisim project subtratorImcompleto.circ as structural Verilog: 1 circuit, main circuit main
module main (
  input  a,
  input  b,
  output Diff,
  output Bout
);

  wire not_1_out;

  not not_1 (not_1_out, a);
  xor xor_1 (Diff, a, b);
  and and_1 (Bout, not_1_out, b);
endmodule
